// Logisim project RealAlu.circ as structural Verilog: 22 circuits, main circuit ArithUnit
module ArithUnit (
  input  a0,
  input  a1,
  input  a2,
  input  a3,
  input  a4,
  input  a5,
  input  a6,
  input  a7,
  input  b0,
  input  b1,
  input  b2,
  input  b3,
  input  b4,
  input  b5,
  input  b6,
  input  b7,
  input  [3:0] Operation,
  output [7:0] A,
  output V,
  output C,
  output Z,
  output N
);

  wire arith_unit_operation_select_1_ablank, arith_unit_operation_select_1_decrem,
       arith_unit_operation_select_1_increm, arith_unit_operation_select_1_somma,
       arith_unit_operation_select_1_sottrazione, b_decrement_1_carry, b_increment_1_carry, button_1_out,
       cpl2_1_over, intel_adder_inside_1_resto, or_2_out, processor_enabler_1_out0, processor_enabler_1_out1,
       processor_enabler_1_out2, processor_enabler_1_out3, processor_enabler_1_out4,
       processor_enabler_1_out5, processor_enabler_1_out6, processor_enabler_1_out7,
       processor_enabler_2_out0, processor_enabler_2_out1, processor_enabler_2_out2,
       processor_enabler_2_out3, processor_enabler_2_out4, processor_enabler_2_out5,
       processor_enabler_2_out6, processor_enabler_2_out7, processor_enabler_3_out0,
       processor_enabler_3_out1, processor_enabler_3_out2, processor_enabler_3_out3,
       processor_enabler_3_out4, processor_enabler_3_out5, processor_enabler_3_out6,
       processor_enabler_3_out7, processor_enabler_4_out0, processor_enabler_4_out1,
       processor_enabler_4_out2, processor_enabler_4_out3, processor_enabler_4_out4,
       processor_enabler_4_out5, processor_enabler_4_out6, processor_enabler_4_out7,
       processor_enabler_aux_1_out0, processor_enabler_aux_1_out1, processor_enabler_aux_1_out2,
       processor_enabler_aux_1_out3, processor_enabler_aux_1_out4, processor_enabler_aux_1_out5,
       processor_enabler_aux_1_out6, processor_enabler_aux_1_out7, processor_enabler_aux_2_out0,
       processor_enabler_aux_2_out1, processor_enabler_aux_2_out2, processor_enabler_aux_2_out3,
       processor_enabler_aux_2_out4, processor_enabler_aux_2_out5, processor_enabler_aux_2_out6,
       processor_enabler_aux_2_out7;
  wire [7:0] a_1_a, b_decrement_1_risultato, b_increment_1_b_1, cpl2_1_y0, intel_adder_inside_1_y0;

  Button button_1 (.out(button_1_out));
  Arith_Unit_Operation_Select arith_unit_operation_select_1 (
    ._0(Operation[0]), ._1(Operation[1]), ._2(Operation[2]), ._3(Operation[3]),
    .Somma(arith_unit_operation_select_1_somma), .Sottrazione(arith_unit_operation_select_1_sottrazione),
    .Increm(arith_unit_operation_select_1_increm), .Decrem(arith_unit_operation_select_1_decrem),
    .aBlank(arith_unit_operation_select_1_ablank));
  A a_1 (.in_1({a7, a6, a5, a4, a3, a2, a1, a0}), .in_2(arith_unit_operation_select_1_ablank), .A(a_1_a));
  Processor_Enabler processor_enabler_1 (
    .Processor_Check(arith_unit_operation_select_1_somma), .IN0(a0), .IN1(a1), .IN2(a2), .IN3(a3), .IN4(a4),
    .IN5(a5), .IN6(a6), .IN7(a7), .OUT0(processor_enabler_1_out0), .OUT1(processor_enabler_1_out1),
    .OUT2(processor_enabler_1_out2), .OUT3(processor_enabler_1_out3), .OUT4(processor_enabler_1_out4),
    .OUT5(processor_enabler_1_out5), .OUT6(processor_enabler_1_out6), .OUT7(processor_enabler_1_out7));
  Intel_Adder_Inside intel_adder_inside_1 (
    .c(button_1_out), .a0(processor_enabler_1_out0), .a1(processor_enabler_1_out1),
    .a2(processor_enabler_1_out2), .a3(processor_enabler_1_out3), .a4(processor_enabler_1_out4),
    .a5(processor_enabler_1_out5), .b0(processor_enabler_aux_1_out0), .a6(processor_enabler_1_out6),
    .b1(processor_enabler_aux_1_out1), .a7(processor_enabler_1_out7), .b2(processor_enabler_aux_1_out2),
    .b4(processor_enabler_aux_1_out4), .b5(processor_enabler_aux_1_out5), .b3(processor_enabler_aux_1_out3),
    .b6(processor_enabler_aux_1_out6), .b7(processor_enabler_aux_1_out7), .Resto(intel_adder_inside_1_resto),
    .y0(intel_adder_inside_1_y0[0]), .y1(intel_adder_inside_1_y0[1]), .y2(intel_adder_inside_1_y0[2]),
    .y3(intel_adder_inside_1_y0[3]), .y4(intel_adder_inside_1_y0[4]), .y5(intel_adder_inside_1_y0[5]),
    .y6(intel_adder_inside_1_y0[6]), .y7(intel_adder_inside_1_y0[7]));
  Processor_Enabler_AUX processor_enabler_aux_1 (
    .Processor_Check(arith_unit_operation_select_1_somma), .IN0(b0), .IN1(b1), .IN2(b2), .IN3(b3), .IN4(b4),
    .IN5(b5), .IN6(b6), .IN7(b7), .OUT0(processor_enabler_aux_1_out0), .OUT1(processor_enabler_aux_1_out1),
    .OUT2(processor_enabler_aux_1_out2), .OUT3(processor_enabler_aux_1_out3),
    .OUT4(processor_enabler_aux_1_out4), .OUT5(processor_enabler_aux_1_out5),
    .OUT6(processor_enabler_aux_1_out6), .OUT7(processor_enabler_aux_1_out7));
  Processor_Enabler processor_enabler_2 (
    .Processor_Check(arith_unit_operation_select_1_sottrazione), .IN0(a0), .IN1(a1), .IN2(a2), .IN3(a3),
    .IN4(a4), .IN5(a5), .IN6(a6), .IN7(a7), .OUT0(processor_enabler_2_out0), .OUT1(processor_enabler_2_out1),
    .OUT2(processor_enabler_2_out2), .OUT3(processor_enabler_2_out3), .OUT4(processor_enabler_2_out4),
    .OUT5(processor_enabler_2_out5), .OUT6(processor_enabler_2_out6), .OUT7(processor_enabler_2_out7));
  Cpl2 cpl2_1 (
    .a0(processor_enabler_2_out0), .a1(processor_enabler_2_out1), .a2(processor_enabler_2_out2),
    .a3(processor_enabler_2_out3), .a4(processor_enabler_2_out4), .a5(processor_enabler_2_out5),
    .a6(processor_enabler_2_out6), .a7(processor_enabler_2_out7), .b0(processor_enabler_aux_2_out0),
    .b1(processor_enabler_aux_2_out1), .b2(processor_enabler_aux_2_out2), .b3(processor_enabler_aux_2_out3),
    .b4(processor_enabler_aux_2_out4), .b5(processor_enabler_aux_2_out5), .b6(processor_enabler_aux_2_out6),
    .b7(processor_enabler_aux_2_out7), .y0(cpl2_1_y0[0]), .y1(cpl2_1_y0[1]), .y2(cpl2_1_y0[2]),
    .y3(cpl2_1_y0[3]), .y4(cpl2_1_y0[4]), .y5(cpl2_1_y0[5]), .y6(cpl2_1_y0[6]), .y7(cpl2_1_y0[7]),
    .c(button_1_out), .OVER(cpl2_1_over));
  Processor_Enabler_AUX processor_enabler_aux_2 (
    .Processor_Check(arith_unit_operation_select_1_sottrazione), .IN0(b0), .IN1(b1), .IN2(b2), .IN3(b3),
    .IN4(b4), .IN5(b5), .IN6(b6), .IN7(b7), .OUT0(processor_enabler_aux_2_out0),
    .OUT1(processor_enabler_aux_2_out1), .OUT2(processor_enabler_aux_2_out2),
    .OUT3(processor_enabler_aux_2_out3), .OUT4(processor_enabler_aux_2_out4),
    .OUT5(processor_enabler_aux_2_out5), .OUT6(processor_enabler_aux_2_out6),
    .OUT7(processor_enabler_aux_2_out7));
  Processor_Enabler processor_enabler_3 (
    .Processor_Check(arith_unit_operation_select_1_increm), .IN0(b0), .IN1(b1), .IN2(b2), .IN3(b3), .IN4(b4),
    .IN5(b5), .IN6(b6), .IN7(b7), .OUT0(processor_enabler_3_out0), .OUT1(processor_enabler_3_out1),
    .OUT2(processor_enabler_3_out2), .OUT3(processor_enabler_3_out3), .OUT4(processor_enabler_3_out4),
    .OUT5(processor_enabler_3_out5), .OUT6(processor_enabler_3_out6), .OUT7(processor_enabler_3_out7));
  B_increment b_increment_1 (
    .Carry(b_increment_1_carry), .B_1(b_increment_1_b_1), ._0(processor_enabler_3_out0),
    .in_2(processor_enabler_3_out1), .in_3(processor_enabler_3_out2), .in_4(processor_enabler_3_out3),
    .in_5(processor_enabler_3_out4), .in_6(processor_enabler_3_out5), .in_7(processor_enabler_3_out6),
    .in_8(processor_enabler_3_out7), .in_9(arith_unit_operation_select_1_increm));
  assign A = intel_adder_inside_1_y0 | cpl2_1_y0 | b_increment_1_b_1 | b_decrement_1_risultato | a_1_a;  // OR_Gate or_1, 8 bits wide
  or or_2 (or_2_out, intel_adder_inside_1_resto, cpl2_1_over, b_increment_1_carry, b_decrement_1_carry);
  Processor_Enabler processor_enabler_4 (
    .Processor_Check(arith_unit_operation_select_1_decrem), .IN0(b0), .IN1(b1), .IN2(b2), .IN3(b3), .IN4(b4),
    .IN5(b5), .IN6(b6), .IN7(b7), .OUT0(processor_enabler_4_out0), .OUT1(processor_enabler_4_out1),
    .OUT2(processor_enabler_4_out2), .OUT3(processor_enabler_4_out3), .OUT4(processor_enabler_4_out4),
    .OUT5(processor_enabler_4_out5), .OUT6(processor_enabler_4_out6), .OUT7(processor_enabler_4_out7));
  B_decrement b_decrement_1 (
    .Risultato(b_decrement_1_risultato), .Carry(b_decrement_1_carry), ._0(processor_enabler_4_out0),
    .in_2(processor_enabler_4_out1), .in_3(processor_enabler_4_out2), .in_4(processor_enabler_4_out3),
    .in_5(processor_enabler_4_out4), .in_6(processor_enabler_4_out5), .in_7(processor_enabler_4_out6),
    .in_8(processor_enabler_4_out7), .Abilit(arith_unit_operation_select_1_decrem));
  Arith_Status_Check arith_status_check_1 (.in_1(or_2_out), .in_2(A), .V(V), .C(C), .Z(Z), .N(N));
endmodule

module Cpl2 (
  input  a0,
  input  a1,
  input  a2,
  input  a3,
  input  a4,
  input  a5,
  input  a6,
  input  a7,
  input  b0,
  input  c,
  input  b1,
  input  b2,
  input  b3,
  input  b4,
  input  b5,
  input  b6,
  input  b7,
  output OVER,
  output y0,
  output y1,
  output y2,
  output y3,
  output y4,
  output y5,
  output y6,
  output y7
);

  wire intel_adder_inside_1_y0, intel_adder_inside_1_y1, intel_adder_inside_1_y2, intel_adder_inside_1_y3,
       intel_adder_inside_1_y4, intel_adder_inside_1_y5, intel_adder_inside_1_y6, intel_adder_inside_1_y7,
       not_1_out, not_2_out, not_3_out, not_4_out, not_5_out, not_6_out, not_7_out, not_8_out;

  not not_1 (not_1_out, b0);
  not not_2 (not_2_out, b1);
  not not_3 (not_3_out, b2);
  not not_4 (not_4_out, b3);
  not not_5 (not_5_out, b4);
  not not_6 (not_6_out, b5);
  not not_7 (not_7_out, b6);
  not not_8 (not_8_out, b7);
  Intel_Adder_Inside intel_adder_inside_1 (
    .c(1'b1), .a0(1'b0), .a1(1'b0), .a2(1'b0), .a3(1'b0), .a4(1'b0), .a5(1'b0), .b0(not_1_out), .a6(1'b0),
    .b1(not_2_out), .a7(1'b0), .b2(not_3_out), .b4(not_5_out), .b5(not_6_out), .b3(not_4_out),
    .b6(not_7_out), .b7(not_8_out), .y0(intel_adder_inside_1_y0), .y1(intel_adder_inside_1_y1),
    .y2(intel_adder_inside_1_y2), .y3(intel_adder_inside_1_y3), .y4(intel_adder_inside_1_y4),
    .y5(intel_adder_inside_1_y5), .y6(intel_adder_inside_1_y6), .y7(intel_adder_inside_1_y7));  // open: Resto
  Intel_Adder_Inside intel_adder_inside_2 (
    .c(c), .a0(a0), .a1(a1), .a2(a2), .a3(a3), .a4(a4), .a5(a5), .b0(intel_adder_inside_1_y0), .a6(a6),
    .b1(intel_adder_inside_1_y1), .a7(a7), .b2(intel_adder_inside_1_y2), .b4(intel_adder_inside_1_y4),
    .b5(intel_adder_inside_1_y5), .b3(intel_adder_inside_1_y3), .b6(intel_adder_inside_1_y6),
    .b7(intel_adder_inside_1_y7), .Resto(OVER), .y0(y0), .y1(y1), .y2(y2), .y3(y3), .y4(y4), .y5(y5),
    .y6(y6), .y7(y7));
endmodule

module and8bit (
  input  [7:0] andA,
  input  [7:0] andB,
  output [7:0] andY
);

  assign andY = andA & andB;  // AND_Gate and_1, 8 bits wide
endmodule

module or8bit (
  input  [7:0] orA,
  input  [7:0] orB,
  output [7:0] orY
);

  assign orY = orA | orB;  // OR_Gate or_1, 8 bits wide
endmodule

module not8bit (
  input  [7:0] notA,
  input  enableA,
  input  [7:0] notB,
  input  enableA_2,
  output [7:0] out_5
);

  wire [7:0] and_1_out, and_2_out, not_1_out, not_2_out;

  assign not_1_out = ~notA;  // NOT_Gate not_1, 8 bits wide
  assign and_1_out = not_1_out & {8{enableA}};  // AND_Gate and_1, 8 bits wide
  assign not_2_out = ~notB;  // NOT_Gate not_2, 8 bits wide
  assign and_2_out = not_2_out & {8{enableA_2}};  // AND_Gate and_2, 8 bits wide
  assign out_5 = and_1_out | and_2_out;  // OR_Gate or_1, 8 bits wide
endmodule

// Integrated Processor Enabler
module Processor_Enabler (
  input  IN0,
  input  IN1,
  input  IN2,
  input  IN3,
  input  IN4,
  input  IN5,
  input  IN6,
  input  IN7,
  input  Processor_Check,
  output OUT0,
  output OUT1,
  output OUT2,
  output OUT3,
  output OUT4,
  output OUT5,
  output OUT6,
  output OUT7
);

  and and_1 (OUT2, Processor_Check, IN2);
  and and_2 (OUT1, Processor_Check, IN1);
  and and_3 (OUT0, Processor_Check, IN0);
  and and_4 (OUT5, Processor_Check, IN5);
  and and_5 (OUT3, Processor_Check, IN3);
  and and_6 (OUT4, Processor_Check, IN4);
  and and_7 (OUT6, Processor_Check, IN6);
  and and_8 (OUT7, Processor_Check, IN7);
endmodule

// Integrated Processor Enabler
module Processor_Enabler_AUX (
  input  IN0,
  input  IN1,
  input  IN2,
  input  IN3,
  input  IN4,
  input  IN5,
  input  IN6,
  input  IN7,
  input  Processor_Check,
  output OUT0,
  output OUT1,
  output OUT2,
  output OUT3,
  output OUT4,
  output OUT5,
  output OUT6,
  output OUT7
);

  and and_1 (OUT2, Processor_Check, IN2);
  and and_2 (OUT1, Processor_Check, IN1);
  and and_3 (OUT0, Processor_Check, IN0);
  and and_4 (OUT5, Processor_Check, IN5);
  and and_5 (OUT4, Processor_Check, IN4);
  and and_6 (OUT3, Processor_Check, IN3);
  and and_7 (OUT7, Processor_Check, IN7);
  and and_8 (OUT6, Processor_Check, IN6);
endmodule

// OPA
module Operation_Selector (
  input  I0,
  input  I1,
  output S0,
  output S1,
  output S2,
  output S3
);

  wire not_1_out, not_2_out;

  not not_1 (not_1_out, I0);
  not not_2 (not_2_out, I1);
  and and_1 (S0, not_1_out, not_2_out);
  and and_2 (S1, not_1_out, I1);
  and and_3 (S2, not_2_out, I0);
  and and_4 (S3, I1, I0);
endmodule

// Integrated Result Confirmer
module Result_Confirmer (
  input  a0,
  input  a1,
  input  a2,
  input  a3,
  input  a4,
  input  a5,
  input  a6,
  input  a7,
  input  b0,
  input  b1,
  input  b2,
  input  b3,
  input  b4,
  input  b5,
  input  b6,
  input  b7,
  output [7:0] out_17
);

  or or_1 (out_17[0], a0, b0);
  or or_2 (out_17[1], a1, b1);
  or or_3 (out_17[2], a2, b2);
  or or_4 (out_17[3], a3, b3);
  or or_5 (out_17[4], a4, b4);
  or or_6 (out_17[5], a5, b5);
  or or_7 (out_17[6], a6, b6);
  or or_8 (out_17[7], a7, b7);
endmodule

module Intel_Adder_Inside (
  input  c,
  input  a0,
  input  a1,
  input  a2,
  input  a3,
  input  a4,
  input  a5,
  input  b0,
  input  a6,
  input  b1,
  input  a7,
  input  b2,
  input  b4,
  input  b5,
  input  b3,
  input  b6,
  input  b7,
  output Resto,
  output y0,
  output y1,
  output y2,
  output y3,
  output y4,
  output y5,
  output y6,
  output y7
);

  wire n4_bit_adder_processor_1_c_2;

  _4_bit_adder_processor u_4_bit_adder_processor_1 (
    .c(c), .a0(a0), .a1(a1), .a2(a2), .a3(a3), .b0(b0), .b1(b1), .b2(b2), .b3(b3), .s0(y0), .s1(y1), .s2(y2),
    .s3(y3), .C_2(n4_bit_adder_processor_1_c_2));
  _4_bit_adder_processor u_4_bit_adder_processor_2 (
    .c(n4_bit_adder_processor_1_c_2), .a0(a4), .a1(a5), .a2(a6), .a3(a7), .b0(b4), .b1(b5), .b2(b6), .b3(b7),
    .s0(y4), .s1(y5), .s2(y6), .s3(y7), .C_2(Resto));
endmodule

module Full_Adder_Subsystem (
  input  c0,
  input  a,
  input  b,
  output S,
  output C
);

  wire and_1_out, and_2_out, and_3_out, xor_1_out;

  and and_1 (and_1_out, b, a);
  xor xor_1 (xor_1_out, a, b);
  xor xor_2 (S, xor_1_out, c0);
  and and_2 (and_2_out, c0, b);
  and and_3 (and_3_out, c0, a);
  or or_1 (C, and_1_out, and_3_out, and_2_out);
endmodule

module _4_bit_adder_processor (
  input  c,
  input  a0,
  input  a1,
  input  a2,
  input  a3,
  input  b0,
  input  b1,
  input  b2,
  input  b3,
  output s0,
  output s1,
  output s2,
  output s3,
  output C_2
);

  wire full_adder_subsystem_1_c, full_adder_subsystem_2_c, full_adder_subsystem_3_c;

  Full_Adder_Subsystem full_adder_subsystem_1 (.c0(c), .a(a0), .b(b0), .S(s0), .C(full_adder_subsystem_1_c));
  Full_Adder_Subsystem full_adder_subsystem_2 (
    .c0(full_adder_subsystem_1_c), .a(a1), .b(b1), .S(s1), .C(full_adder_subsystem_2_c));
  Full_Adder_Subsystem full_adder_subsystem_3 (
    .c0(full_adder_subsystem_2_c), .a(a2), .b(b2), .S(s2), .C(full_adder_subsystem_3_c));
  Full_Adder_Subsystem full_adder_subsystem_4 (.c0(full_adder_subsystem_3_c), .a(a3), .b(b3), .S(s3), .C(C_2));
endmodule

module exor8bit (
  input  [7:0] exorA,
  input  [7:0] exorB,
  output [7:0] exorY
);

  assign exorY = exorA ^ exorB;  // XOR_Gate xor_1, 8 bits wide
endmodule

module Decoder (
  input  O0,
  input  O1,
  input  O2,
  output I7_2600K,
  output I6,
  output I5,
  output I4,
  output I3,
  output I2,
  output I1,
  output I0
);

  wire not_1_out, not_2_out, not_3_out;

  not not_1 (not_1_out, O0);
  not not_2 (not_2_out, O1);
  not not_3 (not_3_out, O2);
  and and_1 (I7_2600K, O0, O1, O2);
  and and_2 (I6, O0, O1, not_3_out);
  and and_3 (I5, O0, not_2_out, O2);
  and and_4 (I4, O0, not_2_out, not_3_out);
  and and_5 (I3, not_1_out, O1, O2);
  and and_6 (I2, not_1_out, O1, not_3_out);
  and and_7 (I1, not_1_out, not_2_out, O2);
  and and_8 (I0, not_1_out, not_2_out, not_3_out);
endmodule

// Unit Abilitator
module LogicUnit_Abilitator (
  input  [7:0] Ingresso,
  input  Abi,
  output [7:0] Uscita
);

  and and_1 (Uscita[0], Abi, Ingresso[0]);
  and and_2 (Uscita[2], Abi, Ingresso[2]);
  and and_3 (Uscita[1], Abi, Ingresso[1]);
  and and_4 (Uscita[4], Abi, Ingresso[4]);
  and and_5 (Uscita[3], Abi, Ingresso[3]);
  and and_6 (Uscita[5], Abi, Ingresso[5]);
  and and_7 (Uscita[6], Abi, Ingresso[6]);
  and and_8 (Uscita[7], Abi, Ingresso[7]);
endmodule

module LBC_message_displayer (
  input  Clear,
  input  Over,
  output [6:0] out_3,
  output out_4
);

  wire and_1_out, and_2_out, and_3_out, and_4_out, clock_1_out, clock_2_out, j_k_ff_1_qn, j_k_ff_2_qn,
       j_k_ff_3_qn, not_1_out;
  wire [2:0] not_4_out;

  and and_1 (and_1_out, and_2_out, not_1_out);
  not not_1 (not_1_out, and_4_out);
  and and_2 (and_2_out, clock_1_out, Over);
  Clock clock_1 (.out(clock_1_out));
  Clock clock_2 (.out(clock_2_out));
  J_K_Flip_Flop j_k_ff_1 (.J(1'b1), .clk(and_1_out), .K(1'b1), .Qn(j_k_ff_1_qn), .reset(Clear));  // open: Q, preset, en
  not not_2 (not_4_out[2], j_k_ff_3_qn);
  not not_3 (not_4_out[1], j_k_ff_2_qn);
  not not_4 (not_4_out[0], j_k_ff_1_qn);
  J_K_Flip_Flop j_k_ff_2 (
    .J(1'b1), .clk(j_k_ff_1_qn), .K(1'b1), .Qn(j_k_ff_2_qn), .reset(Clear));  // open: Q, preset, en
  ROM #(.addrWidth(3), .dataWidth(7)) rom_1 (.addr(not_4_out), .data(out_3), .sel(1'b1));
  and and_3 (and_3_out, and_1_out, clock_2_out);
  J_K_Flip_Flop j_k_ff_3 (
    .J(1'b1), .clk(j_k_ff_2_qn), .K(1'b1), .Qn(j_k_ff_3_qn), .reset(Clear));  // open: Q, preset, en
  and and_4 (and_4_out, not_4_out[2], not_4_out[1], not_4_out[0]);
  not not_5 (out_4, and_4_out);
  TTY tty_1 (.data(out_3), .clk(and_3_out), .clr(Clear));  // open: we

  // Notes on the sheet:
  //   contents of rom_1 (hex, n*v repeats v):
  //   4f 76 72 6c 6f 61 64 20
endmodule

module Advanced_Status_Displayer (
  input  Maggiore,
  input  Uguale,
  input  Minore,
  input  Clear,
  output [6:0] out_5,
  output out_6
);

  wire and_1_out, and_2_out, and_3_out, clock_1_out, clock_2_out, j_k_ff_1_qn, j_k_ff_2_qn, j_k_ff_3_qn,
       not_1_out;
  wire [2:0] not_2_out;

  and and_1 (and_1_out, clock_1_out, not_1_out);
  not not_1 (not_1_out, and_3_out);
  Clock clock_1 (.out(clock_1_out));
  J_K_Flip_Flop j_k_ff_1 (.J(1'b1), .clk(and_1_out), .K(1'b1), .Qn(j_k_ff_1_qn), .reset(Clear));  // open: Q, preset, en
  Clock clock_2 (.out(clock_2_out));
  not not_2 (not_2_out[0], j_k_ff_1_qn);
  not not_3 (not_2_out[1], j_k_ff_2_qn);
  J_K_Flip_Flop j_k_ff_2 (
    .J(1'b1), .clk(j_k_ff_1_qn), .K(1'b1), .Qn(j_k_ff_2_qn), .reset(Clear));  // open: Q, preset, en
  ROM #(.addrWidth(3), .dataWidth(7)) rom_1 (.addr(not_2_out), .data(out_5), .sel(Maggiore));
  not not_4 (not_2_out[2], j_k_ff_3_qn);
  J_K_Flip_Flop j_k_ff_3 (
    .J(1'b1), .clk(j_k_ff_2_qn), .K(1'b1), .Qn(j_k_ff_3_qn), .reset(Clear));  // open: Q, preset, en
  and and_2 (and_2_out, and_1_out, clock_2_out);
  ROM #(.addrWidth(3), .dataWidth(7)) rom_2 (.addr(not_2_out), .data(out_5), .sel(Uguale));
  and and_3 (and_3_out, not_2_out[2], not_2_out[1], not_2_out[0]);
  not not_5 (out_6, and_3_out);
  TTY tty_1 (.data(out_5), .clk(and_2_out), .clr(Clear));  // open: we
  ROM #(.addrWidth(3), .dataWidth(7)) rom_3 (.addr(not_2_out), .data(out_5), .sel(Minore));

  // Notes on the sheet:
  //   contents of rom_1 (hex, n*v repeats v):
  //   41 20 3e 20 42
  //   contents of rom_2 (hex, n*v repeats v):
  //   41 20 3d 20 42
  //   contents of rom_3 (hex, n*v repeats v):
  //   41 20 3c 20 42
endmodule

// AOS
module Arith_Unit_Operation_Select (
  input  _0,
  input  _1,
  input  _2,
  input  _3,
  output Somma,
  output Sottrazione,
  output Increm,
  output Decrem,
  output aBlank
);

  wire not_1_out, not_2_out, not_3_out, not_4_out, not_5_out, not_6_out, not_7_out, not_8_out;

  not not_1 (not_1_out, _1);
  not not_2 (not_2_out, _3);
  not not_3 (not_3_out, _0);
  not not_4 (not_4_out, _1);
  not not_5 (not_5_out, _2);
  not not_6 (not_6_out, not_1_out);
  not not_7 (not_7_out, _0);
  not not_8 (not_8_out, _3);
  and and_1 (Sottrazione, not_6_out, not_7_out, _2, _1);
  and and_2 (Increm, _0, _2, _1, not_8_out);
  and and_3 (Decrem, not_3_out, not_4_out, not_5_out, _3);
  and and_4 (aBlank, _0, not_5_out, not_4_out, _3);
  and and_5 (Somma, _0, not_1_out, _2, not_2_out);
endmodule

module B_increment (
  input  _0,
  input  in_2,
  input  in_3,
  input  in_4,
  input  in_5,
  input  in_6,
  input  in_7,
  input  in_8,
  input  in_9,
  output Carry,
  output [7:0] B_1
);

  Intel_Adder_Inside intel_adder_inside_1 (
    .c(in_9), .a0(_0), .a1(in_2), .a2(in_3), .a3(in_4), .a4(in_5), .a5(in_6), .b0(1'b0), .a6(in_7),
    .b1(1'b0), .a7(in_8), .b2(1'b0), .b4(1'b0), .b5(1'b0), .b3(1'b0), .b6(1'b0), .b7(1'b0), .Resto(Carry),
    .y0(B_1[0]), .y1(B_1[1]), .y2(B_1[2]), .y3(B_1[3]), .y4(B_1[4]), .y5(B_1[5]), .y6(B_1[6]), .y7(B_1[7]));
endmodule

module B_decrement (
  input  _0,
  input  in_2,
  input  in_3,
  input  in_4,
  input  in_5,
  input  in_6,
  input  in_7,
  input  in_8,
  input  Abilit,
  output [7:0] Risultato,
  output Carry
);

  Cpl2 cpl2_1 (
    .a0(_0), .a1(in_2), .a2(in_3), .a3(in_4), .a4(in_5), .a5(in_6), .a6(in_7), .a7(in_8), .b0(Abilit),
    .b1(1'b0), .b2(1'b0), .b3(1'b0), .b4(1'b0), .b5(1'b0), .b6(1'b0), .b7(1'b0), .y0(Risultato[0]),
    .y1(Risultato[1]), .y2(Risultato[2]), .y3(Risultato[3]), .y4(Risultato[4]), .y5(Risultato[5]),
    .y6(Risultato[6]), .y7(Risultato[7]), .c(1'b0), .OVER(Carry));
endmodule

module A (
  input  [7:0] in_1,
  input  in_2,
  output [7:0] A
);

  assign A = in_1 & {8{in_2}};  // AND_Gate and_1, 8 bits wide
endmodule

module Arith_Status_Check (
  input  in_1,
  input  [7:0] in_2,
  output V,
  output C,
  output Z,
  output N
);

  wire or_1_out;

  xor xor_1 (V, in_1, in_2[7]);
  or or_1 (or_1_out, in_2[0], in_2[1], in_2[2], in_2[3], in_2[4], in_2[5], in_2[6], in_2[7]);
  not not_1 (Z, or_1_out);

  assign C = in_1;
  assign N = in_2[7];
endmodule
